# Fritzing sketch DollyDuino_schematic (saved by Fritzing 0.9.3b)

parts:
  Part2 = Arduino Mega 2560 (Rev3)
  LCD_Keypad_shield_(Snap-on) = LCD Keypad Shield  # not connected
  D2F1 = D2F-FL Omron Snap Action Limit Switch with Level
  D2F2 = D2F-FL Omron Snap Action Limit Switch with Level
  S1 = H-Bridge with L298N
  Reg1 = DC-DC CONVERTER [part_number=80633 package=dc-dc_converter]
  M1 = DC Motor
  X1 = USB Connectors [package=usb-a-h]
  R1 = Resistor [tolerance=±5% resistance=1k package="2010 [SMD]"]
  U1 = 2.5mm Audio Jack [package=stereojack2.5mm_smd]
  Q1 = NPN-Transistor [package="TO92 [THT]"]
  U3 = POT [package=alps_pot]

nets:
  N1: Part2.A15, U3.S
  GND: Part2.GND, D2F1.COM, D2F2.COM, Reg1.IN-, X1.GND, U1.SLEEVE, Q1.E, U3.E
  N2: Part2.5V, Reg1.IN+, X1.VBUS, U3.A
  N3: Part2.D2_PWM, S1.ENA
  N4: Part2.D24, S1.IN1
  N5: Part2.D26, S1.IN2
  N6: Part2.D28, D2F1.NO
  N7: Part2.D30, D2F2.NO
  N8: Part2.D32, R1.Pin_1
  N9: S1.12V, Reg1.OUT+
  N10: S1.GND, Reg1.OUT-
  N11: S1.M1-01, M1.pin_1
  N12: S1.M1-02, S1.M2-01, S1.M2-02, S1.ENB-5V, M1.pin_2
  N13: R1.Pin_0, Q1.B
  N14: U1.RIGHT, Q1.C

notes:
  Analog out from pin 2 (PWM)
  5v in to USB

custom parts:
  LCD Keypad Shield: It consists of a 1602 white character blue backlight LCD. The keypad consists of 5 keys — select, up, right, down and left. To save the digital IO pins, the keypad interface uses only one ADC channel. The key value is read through a 5 stage voltage divider.
  D2F-FL Omron Snap Action Limit Switch with Level: Snap action switch with stainless steel lever.
  H-Bridge with L298N: h-bridge
  DC-DC CONVERTER: WYHP 5A constant current/voltage manufactured by Shenzhen Weiyapuhua Technology Co., Ltd
